// Logisim project add_main.circ as structural Verilog: 10 circuits, main circuit main
module main (
  input  Reset,
  output [31:0] out_2,
  output out_3,
  output [4:0] out_4,
  output [31:0] out_5,
  output out_6,
  output [4:0] out_7,
  output [31:0] out_8
);

  wire _0, beq, bgez, clk, Control_alusrc, Control_memtoreg, j, jal, jr, lbu, RegDst, sb, zero;
  wire [1:0] EXTOp, lbu_op;
  wire [2:0] Control_aluop;
  wire [4:0] multiplexer_1_out;
  wire [7:0] bit_extender_1_out;
  wire [31:0] ALU_out_5, EXT_out_3, GRF_out_9, jal_ra, lbu_1_out_3, multiplexer_3_out, multiplexer_5_out,
       multiplexer_6_out, ram_1_data, rs_rd1, sb_1_store, shifter_1_out;

  Clock clock_1 (.out(clk));
  IFU IFU (
    .Reset(Reset), .Clk(clk), .MIPS(out_2), .zero(zero), .beq(beq), .alu__0(_0), .bgez(bgez), .jal(jal),
    .j(j), .jr(jr), .jal__j(out_2[25:0]), .rs_rd1(rs_rd1), .JAL_ra(jal_ra));
  Multiplexer #(.width(5)) multiplexer_1 (
    .in0(out_2[20:16]), .in1(out_2[15:11]), .out(multiplexer_1_out), .sel(RegDst));  // open: en
  Control Control (
    .RegDst(RegDst), .ALUSrc(Control_alusrc), .MemtoReg(Control_memtoreg), .RegWrite(out_3),
    .MemWrite(out_6), .beq(beq), .EXT_Op(EXTOp), .ALUOp(Control_aluop), .op5(out_2[31]), .op4(out_2[30]),
    .op3(out_2[29]), .op2(out_2[28]), .op1(out_2[27]), .op0(out_2[26]), .fc5(out_2[5]), .fc4(out_2[4]),
    .fc3(out_2[3]), .fc2(out_2[2]), .fc1(out_2[1]), .fc0(out_2[0]), .bgez(bgez), .jal(jal), .j(j), .jr(jr),
    .lbu(lbu), .sb(sb), .in_13(out_2[10:6]));
  Multiplexer #(.width(5)) multiplexer_2 (
    .in0(multiplexer_1_out), .in1({5{1'b1}}), .out(out_4), .sel(jal));  // open: en
  EXT EXT (.in_1(out_2[15:0]), .ExtOp(EXTOp), .out_3(EXT_out_3));
  GRF GRF (
    .clk(clk), .rst(Reset), .in_3(out_3), .A1(out_2[25:21]), .A2(out_2[20:16]), .A3(out_4), .in_7(out_5),
    .out_8(rs_rd1), .out_9(GRF_out_9));
  Multiplexer #(.width(32)) multiplexer_3 (
    .in0(GRF_out_9), .in1(EXT_out_3), .out(multiplexer_3_out), .sel(Control_alusrc));  // open: en
  Bit_Extender #(.in_width(32), .out_width(8)) bit_extender_1 (.in(GRF_out_9), .out(bit_extender_1_out));
  ALU ALU (
    .RS(rs_rd1), .RT_IMM(multiplexer_3_out), .ALUOp(Control_aluop), .out_5(ALU_out_5), .Zero(zero), ._0(_0),
    .shift(out_2[10:6]));
  sb sb_1 (.rt_7_0(bit_extender_1_out), .DM_Data(ram_1_data), .sb_op(lbu_op), .store(sb_1_store));
  Bit_Extender #(.in_width(32), .out_width(2)) bit_extender_2 (.in(ALU_out_5), .out(lbu_op));
  Shifter #(.width(32), .shift("lr")) shifter_1 (.in(ALU_out_5), .\dist (5'b00010), .out(shifter_1_out));
  Multiplexer #(.width(32)) multiplexer_4 (.in0(GRF_out_9), .in1(sb_1_store), .out(out_8), .sel(sb));  // open: en
  Bit_Extender #(.in_width(32), .out_width(5)) bit_extender_3 (.in(shifter_1_out), .out(out_7));
  RAM #(.addrWidth(5), .dataWidth(32), .bus("separate")) ram_1 (
    .addr(out_7), .din(out_8), .data(ram_1_data), .str(out_6), .clk(clk), .clr(Reset));  // open: sel, ld
  Multiplexer #(.width(32)) multiplexer_5 (
    .in0(ram_1_data), .in1(lbu_1_out_3), .out(multiplexer_5_out), .sel(lbu));  // open: en
  lbu lbu_1 (.in_1(ram_1_data), .in_2(lbu_op), .out_3(lbu_1_out_3));
  Multiplexer #(.width(32)) multiplexer_6 (
    .in0(ALU_out_5), .in1(multiplexer_5_out), .out(multiplexer_6_out), .sel(Control_memtoreg));  // open: en
  Multiplexer #(.width(32)) multiplexer_7 (.in0(multiplexer_6_out), .in1(jal_ra), .out(out_5), .sel(jal));  // open: en

  // Other names for the same wires on the sheet: _26_31[5:0] = out_2[31:26]; Instr[31:0] = out_2;
  //   _0_5[5:0] = out_2[5:0]; _0_15[15:0] = out_2[15:0]; jal__j[25:0] = out_2[25:0]; _6_10[4:0] = out_2[10:6];
  //   _11_15[4:0] = out_2[15:11]; _16_20[4:0] = out_2[20:16]; _21_25[4:0] = out_2[25:21]; MemAddr[4:0] = out_7;
  //   MemData[31:0] = out_8; MemWrite = out_6; RegAddr[4:0] = out_4; RegData[31:0] = out_5; RegWrite = out_3;
  //   sb_op[1:0] = lbu_op

  // Notes on the sheet:
  //   func
  //   opcode
  //   RegDst
  //   AluSrc
  //   MemtoReg
  //   RegWrite
  //   MemWrite
  //   ExtOp
  //   ALUOp
  //   bgez
  //   beq
  //   Clk
  //   Reset
  //   RegWrite
  //   A1
  //   A2
  //   A3
  //   WD
  //   imm
  //   ExtOp
  //   RD1
  //   RD2
  //   A
  //   B
  //   ALUOp
  //   C
  //   Zero
  //   >=0
endmodule

module GRF (
  input  clk,
  input  rst,
  input  in_3,
  input  [4:0] A1,
  input  [4:0] A2,
  input  [4:0] A3,
  input  [31:0] in_7,
  output [31:0] out_8,
  output [31:0] out_9
);

  wire [31:0] _01, _02, _02out, _03, _03out, _04, _04out, _05, _05out, _06, _06out, _07, _07out, _08, _08out,
       _09, _09out, _10, _10out, _11, _11out, _12, _12out, _13, _13out, _14, _14out, _15, _15out, _16,
       _16out, _17, _17out, _18, _18out, _19, _19out, _20, _20out, _21, _21out, _22, _22out, _23, _23out,
       _24, _24out, _25, _25out, _26, _26out, _27, _27out, _28, _28out, _29, _29out, _30, _30out, _31,
       _31out, _32, _32out;

  Demultiplexer #(.select(5), .width(32), .tristate("true")) demultiplexer_1 (
    .out0(_01), .out1(_02), .out2(_03), .out3(_04), .out4(_05), .out5(_06), .out6(_07), .out7(_08),
    .out8(_09), .out9(_10), .out10(_11), .out11(_12), .out12(_13), .out13(_14), .out14(_15), .out15(_16),
    .out16(_17), .out17(_18), .out18(_19), .out19(_20), .out20(_21), .out21(_22), .out22(_23), .out23(_24),
    .out24(_25), .out25(_26), .out26(_27), .out27(_28), .out28(_29), .out29(_30), .out30(_31), .out31(_32),
    .in(in_7), .sel(A3));  // open: en
  Register #(.width(32)) register_1 (.D(_01), .en(in_3), .clk(clk), .clr(rst));  // open: Q
  Register #(.width(32)) register_2 (.D(_05), .en(in_3), .Q(_05out), .clk(clk), .clr(rst));
  Register #(.width(32)) register_3 (.D(_09), .en(in_3), .Q(_09out), .clk(clk), .clr(rst));
  Register #(.width(32)) register_4 (.D(_13), .en(in_3), .Q(_13out), .clk(clk), .clr(rst));
  Register #(.width(32)) register_5 (.D(_17), .en(in_3), .Q(_17out), .clk(clk), .clr(rst));
  Register #(.width(32)) register_6 (.D(_21), .en(in_3), .Q(_21out), .clk(clk), .clr(rst));
  Register #(.width(32)) register_7 (.D(_25), .en(in_3), .Q(_25out), .clk(clk), .clr(rst));
  Register #(.width(32)) register_8 (.D(_29), .en(in_3), .Q(_29out), .clk(clk), .clr(rst));
  Register #(.width(32)) register_9 (.D(_02), .en(in_3), .Q(_02out), .clk(clk), .clr(rst));
  Register #(.width(32)) register_10 (.D(_06), .en(in_3), .Q(_06out), .clk(clk), .clr(rst));
  Register #(.width(32)) register_11 (.D(_10), .en(in_3), .Q(_10out), .clk(clk), .clr(rst));
  Register #(.width(32)) register_12 (.D(_14), .en(in_3), .Q(_14out), .clk(clk), .clr(rst));
  Register #(.width(32)) register_13 (.D(_18), .en(in_3), .Q(_18out), .clk(clk), .clr(rst));
  Register #(.width(32)) register_14 (.D(_22), .en(in_3), .Q(_22out), .clk(clk), .clr(rst));
  Register #(.width(32)) register_15 (.D(_26), .en(in_3), .Q(_26out), .clk(clk), .clr(rst));
  Register #(.width(32)) register_16 (.D(_30), .en(in_3), .Q(_30out), .clk(clk), .clr(rst));
  Register #(.width(32)) register_17 (.D(_03), .en(in_3), .Q(_03out), .clk(clk), .clr(rst));
  Register #(.width(32)) register_18 (.D(_07), .en(in_3), .Q(_07out), .clk(clk), .clr(rst));
  Register #(.width(32)) register_19 (.D(_11), .en(in_3), .Q(_11out), .clk(clk), .clr(rst));
  Register #(.width(32)) register_20 (.D(_15), .en(in_3), .Q(_15out), .clk(clk), .clr(rst));
  Register #(.width(32)) register_21 (.D(_19), .en(in_3), .Q(_19out), .clk(clk), .clr(rst));
  Register #(.width(32)) register_22 (.D(_23), .en(in_3), .Q(_23out), .clk(clk), .clr(rst));
  Register #(.width(32)) register_23 (.D(_27), .en(in_3), .Q(_27out), .clk(clk), .clr(rst));
  Register #(.width(32)) register_24 (.D(_31), .en(in_3), .Q(_31out), .clk(clk), .clr(rst));
  Register #(.width(32)) register_25 (.D(_04), .en(in_3), .Q(_04out), .clk(clk), .clr(rst));
  Register #(.width(32)) register_26 (.D(_08), .en(in_3), .Q(_08out), .clk(clk), .clr(rst));
  Register #(.width(32)) register_27 (.D(_12), .en(in_3), .Q(_12out), .clk(clk), .clr(rst));
  Register #(.width(32)) register_28 (.D(_16), .en(in_3), .Q(_16out), .clk(clk), .clr(rst));
  Register #(.width(32)) register_29 (.D(_20), .en(in_3), .Q(_20out), .clk(clk), .clr(rst));
  Register #(.width(32)) register_30 (.D(_24), .en(in_3), .Q(_24out), .clk(clk), .clr(rst));
  Register #(.width(32)) register_31 (.D(_28), .en(in_3), .Q(_28out), .clk(clk), .clr(rst));
  Register #(.width(32)) register_32 (.D(_32), .en(in_3), .Q(_32out), .clk(clk), .clr(rst));
  Multiplexer #(.select(5), .width(32)) multiplexer_1 (
    .in0({32{1'b0}}), .in1(_02out), .in2(_03out), .in3(_04out), .in4(_05out), .in5(_06out), .in6(_07out),
    .in7(_08out), .in8(_09out), .in9(_10out), .in10(_11out), .in11(_12out), .in12(_13out), .in13(_14out),
    .in14(_15out), .in15(_16out), .in16(_17out), .in17(_18out), .in18(_19out), .in19(_20out), .in20(_21out),
    .in21(_22out), .in22(_23out), .in23(_24out), .in24(_25out), .in25(_26out), .in26(_27out), .in27(_28out),
    .in28(_29out), .in29(_30out), .in30(_31out), .in31(_32out), .out(out_8), .sel(A1));  // open: en
  Multiplexer #(.select(5), .width(32)) multiplexer_2 (
    .in0({32{1'b0}}), .in1(_02out), .in2(_03out), .in3(_04out), .in4(_05out), .in5(_06out), .in6(_07out),
    .in7(_08out), .in8(_09out), .in9(_10out), .in10(_11out), .in11(_12out), .in12(_13out), .in13(_14out),
    .in14(_15out), .in15(_16out), .in16(_17out), .in17(_18out), .in18(_19out), .in19(_20out), .in20(_21out),
    .in21(_22out), .in22(_23out), .in23(_24out), .in24(_25out), .in25(_26out), .in26(_27out), .in27(_28out),
    .in28(_29out), .in29(_30out), .in30(_31out), .in31(_32out), .out(out_9), .sel(A2));  // open: en

  // Other names for the same wires on the sheet: WE = in_3

  // Notes on the sheet:
  //   WD
  //   RD1
  //   RD2
endmodule

module ALU (
  input  [31:0] RS,
  input  [31:0] RT_IMM,
  input  [4:0] shift,
  input  [2:0] ALUOp,
  output [31:0] out_5,
  output Zero,
  output _0
);

  wire comparator_1_lt, comparator_2_eq, comparator_2_gt;
  wire [4:0] bit_extender_2_out, bit_extender_3_out;
  wire [31:0] _1, _2, _3, _4, _5, _6, _7, _8;

  Adder #(.width(32)) adder_1 (.a(RS), .b(RT_IMM), .out(_1));  // open: cin, cout
  Subtractor #(.width(32)) subtractor_1 (.a(RS), .b(RT_IMM), .out(_2));  // open: bin, bout
  assign _3 = RS | RT_IMM;  // OR_Gate or_1, 32 bits wide
  assign _4 = RS & RT_IMM;  // AND_Gate and_1, 32 bits wide
  Comparator #(.width(32)) comparator_1 (.a(RS), .b(RT_IMM), .lt(comparator_1_lt));  // open: gt, eq
  assign _5 = {{31{1'b0}}, comparator_1_lt};  // Bit_Extender bit_extender_1
  Shifter #(.width(32)) shifter_1 (.in(RT_IMM), .\dist (bit_extender_2_out), .out(_6));
  Bit_Extender #(.in_width(32), .out_width(5)) bit_extender_2 (.in(RS), .out(bit_extender_2_out));
  Shifter #(.width(32)) shifter_2 (.in(RT_IMM), .\dist (shift), .out(_7));
  Shifter #(.width(32), .shift("ar")) shifter_3 (.in(RT_IMM), .\dist (bit_extender_3_out), .out(_8));
  Bit_Extender #(.in_width(32), .out_width(5)) bit_extender_3 (.in(RS), .out(bit_extender_3_out));
  Comparator #(.width(32)) comparator_2 (
    .a(RS), .b({32{1'b0}}), .gt(comparator_2_gt), .eq(comparator_2_eq));  // open: lt
  or or_2 (_0, comparator_2_gt, comparator_2_eq);
  Multiplexer #(.select(3), .width(32)) multiplexer_1 (
    .in0(_1), .in1(_2), .in2(_3), .in3(_4), .in4(_5), .in5(_6), .in6(_7), .in7(_8), .out(out_5), .sel(ALUOp));  // open: en
  Comparator #(.width(32)) comparator_3 (.a(out_5), .b({32{1'b0}}), .eq(Zero));  // open: gt, lt

  // Notes on the sheet:
  //   A
  //   B
  //   C
endmodule

module EXT (
  input  [15:0] in_1,
  input  [1:0] ExtOp,
  output [31:0] out_3
);

  wire [31:0] bit_extender_1_out, bit_extender_2_out;

  assign bit_extender_1_out = {{16{1'b0}}, in_1};  // Bit_Extender bit_extender_1
  assign bit_extender_2_out = {{16{in_1[15]}}, in_1};  // Bit_Extender bit_extender_2
  Multiplexer #(.select(2), .width(32)) multiplexer_1 (
    .in0(bit_extender_1_out), .in1(bit_extender_2_out), .in2({in_1, {16{1'b0}}}), .out(out_3), .sel(ExtOp));  // open: in3, en

  // Notes on the sheet:
  //   Imm
  //   Imm_out
endmodule

module Control (
  input  op5,
  input  op4,
  input  op3,
  input  op2,
  input  op1,
  input  op0,
  input  fc5,
  input  fc4,
  input  fc3,
  input  fc2,
  input  fc1,
  input  fc0,
  input  [4:0] in_13,
  output jal,
  output lbu,
  output j,
  output jr,
  output sb,
  output RegDst,
  output ALUSrc,
  output MemtoReg,
  output RegWrite,
  output MemWrite,
  output bgez,
  output beq,
  output [1:0] EXT_Op,
  output [2:0] ALUOp
);

  wire addu, lui, lw, nop, not_1_out, not_2_out, not_3_out, not_4_out, not_5_out, not_6_out, not_7_out,
       not_8_out, not_9_out, not_10_out, not_11_out, not_12_out, ori, R_mips, shift, sll, slti, subu, sw;

  // NOT_Gate _0 is placed but not wired
  or or_1 (shift, in_13[0], in_13[1], in_13[2], in_13[3], in_13[4]);
  not not_1 (not_1_out, op5);
  not not_2 (not_2_out, op4);
  not not_3 (not_3_out, op2);
  not not_4 (not_4_out, op3);
  not not_5 (not_5_out, op1);
  not not_6 (not_6_out, op0);
  and and_1 (ori, not_1_out, not_2_out, op3, op2, not_5_out, op0);
  and and_2 (lw, op5, not_2_out, not_4_out, not_3_out, op1, op0);
  and and_3 (sw, op5, not_2_out, op3, not_3_out, op1, op0);
  and and_4 (beq, not_1_out, not_2_out, not_4_out, op2, not_5_out, not_6_out);
  and and_5 (lui, not_1_out, not_2_out, op3, op2, op1, op0);
  and and_6 (R_mips, not_1_out, not_2_out, not_4_out, not_3_out, not_5_out, not_6_out);
  and and_7 (bgez, not_1_out, not_2_out, not_4_out, not_3_out, not_5_out, op0);
  and and_8 (slti, not_1_out, not_2_out, op3, not_3_out, op1, not_6_out);
  and and_9 (jal, not_1_out, not_2_out, not_4_out, not_3_out, op1, op0);
  and and_10 (j, not_1_out, not_2_out, not_4_out, not_3_out, op1, not_6_out);
  and and_11 (lbu, op5, not_2_out, not_4_out, op2, not_5_out, not_6_out);
  and and_12 (sb, op5, not_2_out, op3, not_3_out, not_5_out, not_6_out);
  not not_7 (not_7_out, fc5);
  not not_8 (not_8_out, fc4);
  not not_9 (not_9_out, fc3);
  not not_10 (not_10_out, fc2);
  not not_11 (not_11_out, fc1);
  not not_12 (not_12_out, fc0);
  and and_13 (addu, R_mips, fc5, not_8_out, not_9_out, not_10_out, not_11_out, fc0);
  and and_14 (subu, R_mips, fc5, not_8_out, not_9_out, not_10_out, fc1, fc0);
  and and_15 (nop, R_mips, not_7_out, not_8_out, not_9_out, not_10_out, not_11_out, not_12_out);
  and and_16 (jr, R_mips, not_7_out, not_8_out, fc3, not_10_out, not_11_out, not_12_out);
  and and_17 (sll, R_mips, not_7_out, not_8_out, not_9_out, not_10_out, not_11_out, not_12_out, shift);
  or or_2 (MemtoReg, lbu, lw);
  or or_3 (MemWrite, sw, sb);
  or or_4 (EXT_Op[0], lbu, lw, slti, sw, sb);
  buf or_5 (EXT_Op[1], lui);  // OR_Gate
  or or_6 (ALUOp[0], subu, sll, beq);
  buf or_7 (ALUOp[1], ori);  // OR_Gate
  or or_8 (ALUOp[2], slti, sll);
  or or_9 (RegDst, addu, sll, subu);
  or or_10 (ALUSrc, slti, ori, lw, sw, lui, lbu, sb);
  or or_11 (RegWrite, sll, lbu, ori, lw, lui, addu, subu, slti, jal);
endmodule

module IFU (
  input  Reset,
  input  zero,
  input  jr,
  input  beq,
  input  alu__0,
  input  bgez,
  input  jal,
  input  j,
  input  [25:0] jal__j,
  input  [31:0] rs_rd1,
  input  Clk,
  output [31:0] JAL_ra,
  output [31:0] MIPS
);

  wire and_1_out, and_2_out, comparator_1_eq;
  wire [1:0] nPC_Sel, or_1_out;
  wire [4:0] bit_extender_1_out;
  wire [31:0] \begin , multiplexer_1_out, NPC_npc_npc, shifter_1_out;

  and and_1 (and_1_out, zero, beq);
  and and_2 (and_2_out, alu__0, bgez);
  or or_1 (or_1_out[0], and_1_out, and_2_out);
  or or_2 (or_1_out[1], jal, j);
  assign nPC_Sel = {2{jr}} | or_1_out;  // OR_Gate or_3, 2 bits wide
  NPC NPC (
    .NPC_pc(multiplexer_1_out), .IMM(MIPS[15:0]), .JAL__J(jal__j), .JR(rs_rd1), .NPC_pc4(JAL_ra),
    .NPC_npc(NPC_npc_npc), .nPC_Sel(nPC_Sel));
  Register #(.width(32)) register_1 (.D(NPC_npc_npc), .Q(\begin ), .clk(Clk), .clr(Reset));  // open: en
  Comparator #(.width(32), .mode("unsigned")) comparator_1 (
    .a(\begin ), .b({32{1'b0}}), .eq(comparator_1_eq));  // open: gt, lt
  Multiplexer #(.width(32)) multiplexer_1 (
    .in0(\begin ), .in1(32'h3000), .out(multiplexer_1_out), .sel(comparator_1_eq));  // open: en
  Shifter #(.width(32), .shift("lr")) shifter_1 (.in(multiplexer_1_out), .\dist (5'b00010), .out(shifter_1_out));
  Bit_Extender #(.in_width(32), .out_width(5)) bit_extender_1 (.in(shifter_1_out), .out(bit_extender_1_out));
  ROM #(.addrWidth(5), .dataWidth(32)) rom_1 (.addr(bit_extender_1_out), .data(MIPS));  // open: sel

  // Other names for the same wires on the sheet: imm[15:0] = MIPS[15:0]

  // Notes on the sheet:
  //   PC
  //   contents of rom_1 (hex, n*v repeats v):
  //   3c08ffff 3508ffff 1004821 1109ffff
endmodule

module test (
  output [31:0] out_1,
  output out_2,
  output [4:0] out_3,
  output [31:0] out_4,
  output out_5,
  output halt,
  output [4:0] out_7,
  output [31:0] out_8
);

  wire clock_1_out, comparator_1_gt;
  wire [7:0] counter_1_q;

  Clock clock_1 (.out(clock_1_out));
  Counter counter_1 (.Q(counter_1_q), .carry(halt), .clk(clock_1_out));  // open: load, D, count, clr
  Comparator #(.mode("unsigned")) comparator_1 (.a(8'h4), .b(counter_1_q), .gt(comparator_1_gt));  // open: eq, lt
  main main_1 (
    .Reset(comparator_1_gt), .out_2(out_1), .out_3(out_2), .out_4(out_3), .out_5(out_4), .out_6(out_5),
    .out_7(out_7), .out_8(out_8));
endmodule

module NPC (
  input  [31:0] NPC_pc,
  input  [15:0] IMM,
  input  [25:0] JAL__J,
  input  [1:0] nPC_Sel,
  input  [31:0] JR,
  output [31:0] NPC_pc4,
  output [31:0] NPC_npc
);

  wire [31:0] adder_2_out, bit_extender_1_out, shifter_1_out;

  assign bit_extender_1_out = {{16{IMM[15]}}, IMM};  // Bit_Extender bit_extender_1
  Adder #(.width(32)) adder_1 (.a(NPC_pc), .b(32'h4), .out(NPC_pc4));  // open: cin, cout
  Shifter #(.width(32)) shifter_1 (.in(bit_extender_1_out), .\dist (5'b00010), .out(shifter_1_out));
  Adder #(.width(32)) adder_2 (.a(NPC_pc4), .b(shifter_1_out), .out(adder_2_out));  // open: cin, cout
  Multiplexer #(.select(2), .width(32)) multiplexer_1 (
    .in0(NPC_pc4), .in1(adder_2_out), .in2({NPC_pc4[31:28], JAL__J, 2'b00}), .in3(JR), .out(NPC_npc),
    .sel(nPC_Sel));  // open: en
endmodule

module lbu (
  input  [31:0] in_1,
  input  [1:0] in_2,
  output [31:0] out_3
);

  wire [7:0] multiplexer_1_out;

  Multiplexer #(.select(2), .width(8)) multiplexer_1 (
    .in0(in_1[7:0]), .in1(in_1[15:8]), .in2(in_1[23:16]), .in3(in_1[31:24]), .out(multiplexer_1_out),
    .sel(in_2));  // open: en
  assign out_3 = {{24{1'b0}}, multiplexer_1_out};  // Bit_Extender bit_extender_1
endmodule

module sb (
  input  [7:0] rt_7_0,
  input  [31:0] DM_Data,
  input  [1:0] sb_op,
  output [31:0] store
);

  Multiplexer #(.select(2), .width(32)) multiplexer_1 (
    .in0({DM_Data[31:8], rt_7_0}), .in1({DM_Data[31:16], rt_7_0, DM_Data[7:0]}),
    .in2({DM_Data[31:24], rt_7_0, DM_Data[15:0]}), .in3({rt_7_0, DM_Data[23:0]}), .out(store), .sel(sb_op));  // open: en
endmodule
